// Logisim project Snake_Project.circ as structural Verilog: 10 circuits, main circuit main
module main (
);

  wire Clock, clock_1_out, IsKeyPressed;
  wire [6:0] CurrentKey;
  wire [7:0] premain_1_out_4, premain_1_out_5, premain_1_out_6, premain_1_out_7, premain_1_out_8,
       premain_1_out_9, premain_1_out_10, premain_1_out_11;

  PreMain premain_1 (
    .Tact(clock_1_out), .IsKeyPressed(IsKeyPressed), .CurrentKey(CurrentKey), .Clock(Clock),
    .out_4(premain_1_out_4), .out_5(premain_1_out_5), .out_6(premain_1_out_6), .out_7(premain_1_out_7),
    .out_8(premain_1_out_8), .out_9(premain_1_out_9), .out_10(premain_1_out_10), .out_11(premain_1_out_11));  // open: out_13
  DotMatrix #(.matrixcols(8), .matrixrows(8)) dotmatrix_1 (
    .col0(premain_1_out_4), .col1(premain_1_out_5), .col2(premain_1_out_6), .col3(premain_1_out_7),
    .col4(premain_1_out_8), .col5(premain_1_out_9), .col6(premain_1_out_10), .col7(premain_1_out_11));
  Clock clock_1 (.out(clock_1_out));
  Keyboard keyboard_1 (.clk(Clock), .avail(IsKeyPressed), .data(CurrentKey));  // open: re, clr
endmodule

module GetYPositions (
  input  [2:0] HeadYPos,
  input  Clock,
  input  [3:0] Condition,
  output [7:0] CurrentFirstPos8bit,
  output [2:0] CurrentFirstPos3bit,
  output [7:0] CurrentSecondPos8bit,
  output [2:0] CurrentSecondPos3bit,
  output [7:0] CurrentThirdPos8bit,
  output [2:0] CurrentThirdPos3bit,
  output [7:0] CurrentFourthPos8bit,
  output [2:0] CurrentFourthPos3bit,
  output [7:0] CurrentFifthPos8bit,
  output [2:0] CurrentFifthPos3bit
);

  wire comparator_1_gt, comparator_2_gt, comparator_3_gt, comparator_4_gt;

  Decoder #(.select(3), .enable("false")) decoder_1 (
    .out0(CurrentFirstPos8bit[0]), .out1(CurrentFirstPos8bit[1]), .out2(CurrentFirstPos8bit[2]),
    .out3(CurrentFirstPos8bit[3]), .out4(CurrentFirstPos8bit[4]), .out5(CurrentFirstPos8bit[5]),
    .out6(CurrentFirstPos8bit[6]), .out7(CurrentFirstPos8bit[7]), .sel(HeadYPos));
  Decoder #(.select(3), .enable("false")) decoder_2 (
    .out0(CurrentSecondPos8bit[0]), .out1(CurrentSecondPos8bit[1]), .out2(CurrentSecondPos8bit[2]),
    .out3(CurrentSecondPos8bit[3]), .out4(CurrentSecondPos8bit[4]), .out5(CurrentSecondPos8bit[5]),
    .out6(CurrentSecondPos8bit[6]), .out7(CurrentSecondPos8bit[7]), .sel(CurrentSecondPos3bit));
  Decoder #(.select(3), .enable("false")) decoder_3 (
    .out0(CurrentThirdPos8bit[0]), .out1(CurrentThirdPos8bit[1]), .out2(CurrentThirdPos8bit[2]),
    .out3(CurrentThirdPos8bit[3]), .out4(CurrentThirdPos8bit[4]), .out5(CurrentThirdPos8bit[5]),
    .out6(CurrentThirdPos8bit[6]), .out7(CurrentThirdPos8bit[7]), .sel(CurrentThirdPos3bit));
  Decoder #(.select(3), .enable("false")) decoder_4 (
    .out0(CurrentFourthPos8bit[0]), .out1(CurrentFourthPos8bit[1]), .out2(CurrentFourthPos8bit[2]),
    .out3(CurrentFourthPos8bit[3]), .out4(CurrentFourthPos8bit[4]), .out5(CurrentFourthPos8bit[5]),
    .out6(CurrentFourthPos8bit[6]), .out7(CurrentFourthPos8bit[7]), .sel(CurrentFourthPos3bit));
  Decoder #(.select(3), .enable("false")) decoder_5 (
    .out0(CurrentFifthPos8bit[0]), .out1(CurrentFifthPos8bit[1]), .out2(CurrentFifthPos8bit[2]),
    .out3(CurrentFifthPos8bit[3]), .out4(CurrentFifthPos8bit[4]), .out5(CurrentFifthPos8bit[5]),
    .out6(CurrentFifthPos8bit[6]), .out7(CurrentFifthPos8bit[7]), .sel(CurrentFifthPos3bit));
  Comparator #(.width(4), .mode("unsigned")) comparator_1 (
    .a(Condition), .b(4'b0001), .gt(comparator_1_gt));  // open: eq, lt
  Register #(.width(3)) register_1 (
    .D(HeadYPos), .en(comparator_1_gt), .Q(CurrentSecondPos3bit), .clk(Clock));  // open: clr
  Register #(.width(3)) register_2 (
    .D(CurrentSecondPos3bit), .en(comparator_2_gt), .Q(CurrentThirdPos3bit), .clk(Clock));  // open: clr
  Comparator #(.width(4), .mode("unsigned")) comparator_2 (
    .a(Condition), .b(4'b0011), .gt(comparator_2_gt));  // open: eq, lt
  Register #(.width(3)) register_3 (
    .D(CurrentThirdPos3bit), .en(comparator_3_gt), .Q(CurrentFourthPos3bit), .clk(Clock));  // open: clr
  Comparator #(.width(4), .mode("unsigned")) comparator_3 (
    .a(Condition), .b(4'b0101), .gt(comparator_3_gt));  // open: eq, lt
  Register #(.width(3)) register_4 (
    .D(CurrentFourthPos3bit), .en(comparator_4_gt), .Q(CurrentFifthPos3bit), .clk(Clock));  // open: clr
  Comparator #(.width(4), .mode("unsigned")) comparator_4 (
    .a(Condition), .b(4'b0111), .gt(comparator_4_gt));  // open: eq, lt

  assign CurrentFirstPos3bit = HeadYPos;
endmodule

module GetXPositions (
  input  [2:0] HeadXPos,
  input  Clock,
  input  [3:0] Condition,
  output [2:0] CurrentSecondPos3bit,
  output [2:0] CurrentThirdPos3bit,
  output [2:0] CurrentFourthPos3bit,
  output [2:0] CurrentFifthPos3bit
);

  wire comparator_1_gt, comparator_2_gt, comparator_3_gt, comparator_4_gt;

  Comparator #(.width(4), .mode("unsigned")) comparator_1 (
    .a(Condition), .b(4'b0001), .gt(comparator_1_gt));  // open: eq, lt
  Register #(.width(3)) register_1 (
    .D(HeadXPos), .en(comparator_1_gt), .Q(CurrentSecondPos3bit), .clk(Clock));  // open: clr
  Comparator #(.width(4), .mode("unsigned")) comparator_2 (
    .a(Condition), .b(4'b0011), .gt(comparator_2_gt));  // open: eq, lt
  Register #(.width(3)) register_2 (
    .D(CurrentSecondPos3bit), .en(comparator_2_gt), .Q(CurrentThirdPos3bit), .clk(Clock));  // open: clr
  Comparator #(.width(4), .mode("unsigned")) comparator_3 (
    .a(Condition), .b(4'b0101), .gt(comparator_3_gt));  // open: eq, lt
  Register #(.width(3)) register_3 (
    .D(CurrentThirdPos3bit), .en(comparator_3_gt), .Q(CurrentFourthPos3bit), .clk(Clock));  // open: clr
  Comparator #(.width(4), .mode("unsigned")) comparator_4 (
    .a(Condition), .b(4'b0111), .gt(comparator_4_gt));  // open: eq, lt
  Register #(.width(3)) register_4 (
    .D(CurrentFourthPos3bit), .en(comparator_4_gt), .Q(CurrentFifthPos3bit), .clk(Clock));  // open: clr
endmodule

// CLD
module ConditionLevelDeterminer (
  input  AssemblerRes,
  input  Clock,
  input  [3:0] Condition,
  input  [1:0] Level,
  output [3:0] Condition_2,
  output [1:0] Level_2,
  output IsLevelChanged
);

  wire [1:0] adder_3_out;
  wire [3:0] adder_1_out, adder_2_out, multiplexer_1_out, multiplexer_2_out;

  Multiplexer #(.width(4), .enable("false")) multiplexer_1 (
    .in0(4'b0001), .in1(4'b0000), .out(multiplexer_1_out), .sel(Condition[0]));
  Adder #(.width(4)) adder_1 (.a({3'b000, AssemblerRes}), .b(multiplexer_1_out), .out(adder_1_out));  // open: cin, cout
  Adder #(.width(4)) adder_2 (.a(adder_1_out), .b(Condition), .out(adder_2_out));  // open: cin, cout
  Multiplexer #(.width(4), .enable("false")) multiplexer_2 (
    .in0(adder_2_out), .in1(4'b0000), .out(multiplexer_2_out), .sel(IsLevelChanged));
  Comparator #(.width(4), .mode("unsigned")) comparator_1 (
    .a(Condition), .b(4'b1001), .gt(IsLevelChanged));  // open: eq, lt
  Register #(.width(4)) register_1 (.D(multiplexer_2_out), .en(1'b1), .Q(Condition_2), .clk(Clock));  // open: clr
  Register #(.width(2)) register_2 (.D(adder_3_out), .en(1'b1), .Q(Level_2), .clk(Clock));  // open: clr
  Adder #(.width(2)) adder_3 (.a({1'b0, IsLevelChanged}), .b(Level), .out(adder_3_out));  // open: cin, cout
endmodule

// BitsFromPos
module GetBitsFromPos (
  input  [3:0] CheckValue,
  input  [3:0] Condition,
  input  [2:0] XPos3bit,
  input  [7:0] YPos8bit,
  output [7:0] out_5,
  output [7:0] out_6,
  output [7:0] out_7,
  output [7:0] out_8,
  output [7:0] out_9,
  output [7:0] out_10,
  output [7:0] out_11,
  output [7:0] out_12
);

  wire comparator_1_gt;
  wire [3:0] multiplexer_1_out;

  Comparator #(.width(4), .mode("unsigned")) comparator_1 (
    .a(Condition), .b(CheckValue), .gt(comparator_1_gt));  // open: eq, lt
  Multiplexer #(.width(4), .enable("false")) multiplexer_1 (
    .in0(4'b1000), .in1({1'b0, XPos3bit}), .out(multiplexer_1_out), .sel(comparator_1_gt));
  Demultiplexer #(.select(4), .width(8), .enable("false")) demultiplexer_1 (
    .out0(out_5), .out1(out_6), .out2(out_7), .out3(out_8), .out4(out_9), .out5(out_10), .out6(out_11),
    .out7(out_12), .in(YPos8bit), .sel(multiplexer_1_out));  // open: out8, out9, out10, out11, out12, out13, out14, out15
endmodule

// AppleCoordGen
module AppleCoordinatesGenerator (
  input  Clock,
  input  [1:0] Level,
  input  [3:0] Condition,
  output [2:0] AppleYPos,
  output [2:0] AppleXPos,
  output [7:0] out1,
  output [7:0] out2,
  output [7:0] out3,
  output [7:0] out4,
  output [7:0] out5,
  output [7:0] out6,
  output [7:0] out7,
  output [7:0] out8
);

  wire not_1_out, not_2_out;
  wire [2:0] AppleXPos3bit0Level, AppleXPos3bit1Level, AppleXPos3bit2Level, AppleYPos3bit0Level,
       AppleYPos3bit1Level, AppleYPos3bit2Level, multiplexer_1_out, multiplexer_2_out, Selector;
  wire [7:0] decoder_1_out0, out1_t, out2_t, out3_t, out4_t, out5_t, out6_t, out7_t, out8_t;

  Random #(.width(3)) random_1 (.clk(Clock), .next(1'b1), .out(Selector));  // open: clr
  Transistor transistor_1 (.in(out1_t[0]), .out(out1[0]), .gate(out1_t[0]));
  Transistor transistor_2 (.in(out1_t[1]), .out(out1[1]), .gate(out1_t[1]));
  Transistor transistor_3 (.in(out1_t[2]), .out(out1[2]), .gate(out1_t[2]));
  Transistor transistor_4 (.in(out1_t[3]), .out(out1[3]), .gate(out1_t[3]));
  Transistor #(.gate("br")) transistor_5 (.in(out1_t[4]), .out(out1[4]), .gate(out1_t[4]));
  Transistor #(.gate("br")) transistor_6 (.in(out1_t[5]), .out(out1[5]), .gate(out1_t[5]));
  Transistor #(.gate("br")) transistor_7 (.in(out1_t[6]), .out(out1[6]), .gate(out1_t[6]));
  Transistor #(.gate("br")) transistor_8 (.in(out1_t[7]), .out(out1[7]), .gate(out1_t[7]));
  Transistor transistor_9 (.in(out5_t[0]), .out(out5[0]), .gate(out5_t[0]));
  Transistor transistor_10 (.in(out5_t[1]), .out(out5[1]), .gate(out5_t[1]));
  Transistor transistor_11 (.in(out5_t[2]), .out(out5[2]), .gate(out5_t[2]));
  Transistor transistor_12 (.in(out5_t[3]), .out(out5[3]), .gate(out5_t[3]));
  Transistor #(.gate("br")) transistor_13 (.in(out5_t[4]), .out(out5[4]), .gate(out5_t[4]));
  Transistor #(.gate("br")) transistor_14 (.in(out5_t[5]), .out(out5[5]), .gate(out5_t[5]));
  Transistor #(.gate("br")) transistor_15 (.in(out5_t[6]), .out(out5[6]), .gate(out5_t[6]));
  Transistor #(.gate("br")) transistor_16 (.in(out5_t[7]), .out(out5[7]), .gate(out5_t[7]));
  Multiplexer #(.select(2), .width(3), .enable("false")) multiplexer_1 (
    .in0(AppleYPos3bit0Level), .in1(AppleYPos3bit1Level), .in2(AppleYPos3bit2Level), .out(multiplexer_1_out),
    .sel(Level));  // open: in3
  Multiplexer #(.select(2), .width(3), .enable("false")) multiplexer_2 (
    .in0(AppleXPos3bit0Level), .in1(AppleXPos3bit1Level), .in2(AppleXPos3bit2Level), .out(multiplexer_2_out),
    .sel(Level));  // open: in3
  Multiplexer #(.select(3), .width(3), .enable("false")) multiplexer_3 (
    .in0(3'b011), .in1(3'b100), .in2(3'b110), .in3(3'b101), .in4(3'b001), .in5(3'b100), .in6(3'b010),
    .in7(3'b001), .out(AppleXPos3bit0Level), .sel(Selector));
  Multiplexer #(.select(3), .width(3), .enable("false")) multiplexer_4 (
    .in0(3'b000), .in1(3'b010), .in2(3'b101), .in3(3'b110), .in4(3'b111), .in5(3'b001), .in6(3'b100),
    .in7(3'b011), .out(AppleYPos3bit0Level), .sel(Selector));
  Transistor transistor_17 (.in(out2_t[0]), .out(out2[0]), .gate(out2_t[0]));
  Transistor transistor_18 (.in(out2_t[1]), .out(out2[1]), .gate(out2_t[1]));
  Transistor transistor_19 (.in(out2_t[2]), .out(out2[2]), .gate(out2_t[2]));
  Transistor transistor_20 (.in(out2_t[3]), .out(out2[3]), .gate(out2_t[3]));
  Transistor #(.gate("br")) transistor_21 (.in(out2_t[4]), .out(out2[4]), .gate(out2_t[4]));
  Transistor #(.gate("br")) transistor_22 (.in(out2_t[5]), .out(out2[5]), .gate(out2_t[5]));
  Transistor #(.gate("br")) transistor_23 (.in(out2_t[6]), .out(out2[6]), .gate(out2_t[6]));
  Transistor #(.gate("br")) transistor_24 (.in(out2_t[7]), .out(out2[7]), .gate(out2_t[7]));
  Transistor transistor_25 (.in(out6_t[0]), .out(out6[0]), .gate(out6_t[0]));
  Transistor transistor_26 (.in(out6_t[1]), .out(out6[1]), .gate(out6_t[1]));
  Transistor transistor_27 (.in(out6_t[2]), .out(out6[2]), .gate(out6_t[2]));
  Transistor transistor_28 (.in(out6_t[3]), .out(out6[3]), .gate(out6_t[3]));
  Transistor #(.gate("br")) transistor_29 (.in(out6_t[4]), .out(out6[4]), .gate(out6_t[4]));
  Transistor #(.gate("br")) transistor_30 (.in(out6_t[5]), .out(out6[5]), .gate(out6_t[5]));
  Transistor #(.gate("br")) transistor_31 (.in(out6_t[6]), .out(out6[6]), .gate(out6_t[6]));
  Transistor #(.gate("br")) transistor_32 (.in(out6_t[7]), .out(out6[7]), .gate(out6_t[7]));
  not not_1 (not_1_out, Condition[0]);
  not not_2 (not_2_out, Condition[0]);
  Multiplexer #(.select(3), .width(3), .enable("false")) multiplexer_5 (
    .in0(3'b011), .in1(3'b010), .in2(3'b100), .in3(3'b011), .in4(3'b010), .in5(3'b101), .in6(3'b100),
    .in7(3'b100), .out(AppleXPos3bit1Level), .sel(Selector));
  Multiplexer #(.select(3), .width(3), .enable("false")) multiplexer_6 (
    .in0(3'b101), .in1(3'b101), .in2(3'b010), .in3(3'b011), .in4(3'b100), .in5(3'b101), .in6(3'b010),
    .in7(3'b100), .out(AppleYPos3bit1Level), .sel(Selector));
  Decoder #(.select(3), .enable("false")) decoder_1 (
    .out0(decoder_1_out0[0]), .out1(decoder_1_out0[1]), .out2(decoder_1_out0[2]), .out3(decoder_1_out0[3]),
    .out4(decoder_1_out0[4]), .out5(decoder_1_out0[5]), .out6(decoder_1_out0[6]), .out7(decoder_1_out0[7]),
    .sel(AppleYPos));
  Register #(.width(3)) register_1 (.D(multiplexer_1_out), .en(not_1_out), .Q(AppleYPos), .clk(Clock));  // open: clr
  Register #(.width(3)) register_2 (.D(multiplexer_2_out), .en(not_2_out), .Q(AppleXPos), .clk(Clock));  // open: clr
  Demultiplexer #(.select(3), .width(8), .enable("false")) demultiplexer_1 (
    .out0(out1_t), .out1(out2_t), .out2(out3_t), .out3(out4_t), .out4(out5_t), .out5(out6_t), .out6(out7_t),
    .out7(out8_t), .in(decoder_1_out0), .sel(AppleXPos));
  Transistor transistor_33 (.in(out3_t[0]), .out(out3[0]), .gate(out3_t[0]));
  Transistor transistor_34 (.in(out3_t[1]), .out(out3[1]), .gate(out3_t[1]));
  Transistor transistor_35 (.in(out3_t[2]), .out(out3[2]), .gate(out3_t[2]));
  Transistor transistor_36 (.in(out3_t[3]), .out(out3[3]), .gate(out3_t[3]));
  Transistor #(.gate("br")) transistor_37 (.in(out3_t[4]), .out(out3[4]), .gate(out3_t[4]));
  Transistor #(.gate("br")) transistor_38 (.in(out3_t[5]), .out(out3[5]), .gate(out3_t[5]));
  Transistor #(.gate("br")) transistor_39 (.in(out3_t[6]), .out(out3[6]), .gate(out3_t[6]));
  Transistor #(.gate("br")) transistor_40 (.in(out3_t[7]), .out(out3[7]), .gate(out3_t[7]));
  Transistor transistor_41 (.in(out7_t[0]), .out(out7[0]), .gate(out7_t[0]));
  Transistor transistor_42 (.in(out7_t[1]), .out(out7[1]), .gate(out7_t[1]));
  Transistor transistor_43 (.in(out7_t[2]), .out(out7[2]), .gate(out7_t[2]));
  Transistor transistor_44 (.in(out7_t[3]), .out(out7[3]), .gate(out7_t[3]));
  Transistor #(.gate("br")) transistor_45 (.in(out7_t[4]), .out(out7[4]), .gate(out7_t[4]));
  Transistor #(.gate("br")) transistor_46 (.in(out7_t[5]), .out(out7[5]), .gate(out7_t[5]));
  Transistor #(.gate("br")) transistor_47 (.in(out7_t[6]), .out(out7[6]), .gate(out7_t[6]));
  Transistor #(.gate("br")) transistor_48 (.in(out7_t[7]), .out(out7[7]), .gate(out7_t[7]));
  Multiplexer #(.select(3), .width(3), .enable("false")) multiplexer_7 (
    .in0(3'b010), .in1(3'b100), .in2(3'b010), .in3(3'b100), .in4(3'b010), .in5(3'b011), .in6(3'b011),
    .in7(3'b101), .out(AppleXPos3bit2Level), .sel(Selector));
  Multiplexer #(.select(3), .width(3), .enable("false")) multiplexer_8 (
    .in0(3'b100), .in1(3'b101), .in2(3'b010), .in3(3'b011), .in4(3'b010), .in5(3'b101), .in6(3'b010),
    .in7(3'b011), .out(AppleYPos3bit2Level), .sel(Selector));
  Transistor transistor_49 (.in(out4_t[0]), .out(out4[0]), .gate(out4_t[0]));
  Transistor transistor_50 (.in(out4_t[1]), .out(out4[1]), .gate(out4_t[1]));
  Transistor transistor_51 (.in(out4_t[2]), .out(out4[2]), .gate(out4_t[2]));
  Transistor transistor_52 (.in(out4_t[3]), .out(out4[3]), .gate(out4_t[3]));
  Transistor #(.gate("br")) transistor_53 (.in(out4_t[4]), .out(out4[4]), .gate(out4_t[4]));
  Transistor #(.gate("br")) transistor_54 (.in(out4_t[5]), .out(out4[5]), .gate(out4_t[5]));
  Transistor #(.gate("br")) transistor_55 (.in(out4_t[6]), .out(out4[6]), .gate(out4_t[6]));
  Transistor #(.gate("br")) transistor_56 (.in(out4_t[7]), .out(out4[7]), .gate(out4_t[7]));
  Transistor transistor_57 (.in(out8_t[0]), .out(out8[0]), .gate(out8_t[0]));
  Transistor transistor_58 (.in(out8_t[1]), .out(out8[1]), .gate(out8_t[1]));
  Transistor transistor_59 (.in(out8_t[2]), .out(out8[2]), .gate(out8_t[2]));
  Transistor transistor_60 (.in(out8_t[3]), .out(out8[3]), .gate(out8_t[3]));
  Transistor #(.gate("br")) transistor_61 (.in(out8_t[4]), .out(out8[4]), .gate(out8_t[4]));
  Transistor #(.gate("br")) transistor_62 (.in(out8_t[5]), .out(out8[5]), .gate(out8_t[5]));
  Transistor #(.gate("br")) transistor_63 (.in(out8_t[6]), .out(out8[6]), .gate(out8_t[6]));
  Transistor #(.gate("br")) transistor_64 (.in(out8_t[7]), .out(out8[7]), .gate(out8_t[7]));
endmodule

module Processor (
  input  in_1,
  input  [3:0] in_2,
  input  [2:0] HeadX,
  input  [2:0] HeadY,
  input  [2:0] X_second_Pos,
  input  [2:0] Y_second_Pos,
  input  [2:0] X_third_Pos,
  input  [2:0] AppleX,
  input  [2:0] Y_third_Pos,
  input  [2:0] AppleY,
  input  [2:0] X_fourth_Pos,
  input  [2:0] Y_fourth_Pos,
  input  [2:0] X_fifth_Pos,
  input  [2:0] Y_fifth_Pos,
  output YES_NO_APPLE,
  output OSHIBKA,
  output clk
);

  wire and_3_out, and_4_out, and_5_out, and_6_out, and_7_out, and_8_out, and_9_out, and_10_out, and_11_out,
       and_12_out, and_13_out, and_14_out, and_15_out, and_16_out, and_17_out, cdm_8_mark5_1_data_inst, CODE,
       comparator_1_gt, comparator_2_gt, comparator_3_gt, comparator_4_gt, comparator_5_gt, comparator_6_gt,
       comparator_7_gt, comparator_8_gt, DATA, decoder_1_out1, decoder_1_out2, decoder_1_out3,
       decoder_1_out4, decoder_1_out5, decoder_1_out6, decoder_1_out7, decoder_1_out8, decoder_1_out9,
       decoder_1_out10, decoder_1_out11, decoder_1_out12, decoder_1_out13, decoder_1_out14, decoder_1_out15,
       I_Osel, IN_OUT, MEM, nand_1_out, nor_1_out, not_1_out, not_2_out, not_3_out, RAM;
  wire [3:0] I_Oaddr;
  wire [7:0] cdm_8_mark5_1_data_out, cdm_8_mark5_1_pc, cdm_8_mark5_1_r0, cdm_8_mark5_1_r1, cdm_8_mark5_1_r2,
       cdm_8_mark5_1_r3, cdm_8_mark5_1_sp, controlled_buffer_2_out, I_Odat, multiplexer_1_out,
       multiplexer_2_out, multiplexer_3_out, multiplexer_4_out, multiplexer_5_out, multiplexer_6_out,
       multiplexer_7_out, multiplexer_8_out;
  wire [7:1] register_1_q, register_2_q, register_3_q;
  wire [7:4] cdm_8_mark5_1_addr;

  // Probe on in_2
  and and_1 (I_Osel, not_1_out, in_1, DATA);
  Decoder #(.select(4)) decoder_1 (
    .out1(decoder_1_out1), .out2(decoder_1_out2), .out3(decoder_1_out3), .out4(decoder_1_out4),
    .out5(decoder_1_out5), .out6(decoder_1_out6), .out7(decoder_1_out7), .out8(decoder_1_out8),
    .out9(decoder_1_out9), .out10(decoder_1_out10), .out11(decoder_1_out11), .out12(decoder_1_out12),
    .out13(decoder_1_out13), .out14(decoder_1_out14), .out15(decoder_1_out15), .sel(I_Oaddr));  // open: out0, en
  // Probe on cdm_8_mark5_1_r0
  // Probe on cdm_8_mark5_1_r1
  // Probe on cdm_8_mark5_1_r2
  // Probe on cdm_8_mark5_1_r3
  not not_1 (not_1_out, nand_1_out);
  and and_2 (RAM, nand_1_out, DATA);
  // Probe on cdm_8_mark5_1_pc
  // Probe on cdm_8_mark5_1_sp
  CdM_8_mark5 cdm_8_mark5_1 (
    .clock(in_1), .addr({cdm_8_mark5_1_addr, I_Oaddr}), .mem_read(IN_OUT), .mem_cycle(MEM),
    .data_inst(cdm_8_mark5_1_data_inst), .data_out(cdm_8_mark5_1_data_out),
    .data_in(controlled_buffer_2_out), .r0(cdm_8_mark5_1_r0), .r1(cdm_8_mark5_1_r1), .r2(cdm_8_mark5_1_r2),
    .r3(cdm_8_mark5_1_r3), .PC(cdm_8_mark5_1_pc), .SP(cdm_8_mark5_1_sp));  // open: PS, IAck, IRQ, vec
  Decoder decoder_2 (.out0(CODE), .out1(DATA), .sel(cdm_8_mark5_1_data_inst), .en(MEM));
  assign I_Odat = not_2_out ? cdm_8_mark5_1_data_out : 8'bz;  // Controlled_Buffer controlled_buffer_1
  not not_2 (not_2_out, IN_OUT);
  assign controlled_buffer_2_out = IN_OUT ? I_Odat : 8'bz;  // Controlled_Buffer controlled_buffer_2
  nand nand_1 (nand_1_out, cdm_8_mark5_1_addr[4], cdm_8_mark5_1_addr[5], cdm_8_mark5_1_addr[6], cdm_8_mark5_1_addr[7]);
  and and_3 (and_3_out, decoder_1_out1, ~IN_OUT, I_Osel);  // AND_Gate
  and and_4 (and_4_out, decoder_1_out2, IN_OUT, I_Osel);
  and and_5 (and_5_out, decoder_1_out3, IN_OUT, I_Osel);
  and and_6 (and_6_out, decoder_1_out4, IN_OUT, I_Osel);
  and and_7 (and_7_out, decoder_1_out5, IN_OUT, I_Osel);
  and and_8 (and_8_out, decoder_1_out6, IN_OUT, I_Osel);
  and and_9 (and_9_out, decoder_1_out7, IN_OUT, I_Osel);
  and and_10 (and_10_out, decoder_1_out8, IN_OUT, I_Osel);
  and and_11 (and_11_out, decoder_1_out9, IN_OUT, I_Osel);
  and and_12 (and_12_out, decoder_1_out10, IN_OUT, I_Osel);
  and and_13 (and_13_out, decoder_1_out11, IN_OUT, I_Osel);
  and and_14 (and_14_out, decoder_1_out12, IN_OUT, I_Osel);
  and and_15 (and_15_out, decoder_1_out13, IN_OUT, I_Osel);
  and and_16 (and_16_out, decoder_1_out14, ~IN_OUT, I_Osel);  // AND_Gate
  and and_17 (and_17_out, decoder_1_out15, ~IN_OUT, I_Osel);  // AND_Gate
  assign I_Odat = and_8_out ? multiplexer_3_out : 8'bz;  // Controlled_Buffer controlled_buffer_3
  assign I_Odat = and_9_out ? multiplexer_4_out : 8'bz;  // Controlled_Buffer controlled_buffer_4
  assign I_Odat = and_10_out ? multiplexer_5_out : 8'bz;  // Controlled_Buffer controlled_buffer_5
  assign I_Odat = and_11_out ? multiplexer_6_out : 8'bz;  // Controlled_Buffer controlled_buffer_6
  assign I_Odat = and_12_out ? multiplexer_7_out : 8'bz;  // Controlled_Buffer controlled_buffer_7
  assign I_Odat = and_13_out ? multiplexer_8_out : 8'bz;  // Controlled_Buffer controlled_buffer_8
  assign I_Odat = and_14_out ? {{5{1'b0}}, AppleX} : 8'bz;  // Controlled_Buffer controlled_buffer_9
  assign I_Odat = and_15_out ? {{5{1'b0}}, AppleY} : 8'bz;  // Controlled_Buffer controlled_buffer_10
  ROM rom_1 (.addr({cdm_8_mark5_1_addr, I_Oaddr}), .data(I_Odat), .sel(CODE));
  RAM ram_1 (
    .addr({cdm_8_mark5_1_addr, I_Oaddr}), .data(I_Odat), .sel(RAM), .clk(not_3_out), .ld(IN_OUT));  // open: clr
  not not_3 (not_3_out, in_1);
  assign I_Odat = and_4_out ? {{5{1'b0}}, HeadX} : 8'bz;  // Controlled_Buffer controlled_buffer_11
  assign I_Odat = and_5_out ? {{5{1'b0}}, HeadY} : 8'bz;  // Controlled_Buffer controlled_buffer_12
  assign I_Odat = and_6_out ? multiplexer_1_out : 8'bz;  // Controlled_Buffer controlled_buffer_13
  assign I_Odat = and_7_out ? multiplexer_2_out : 8'bz;  // Controlled_Buffer controlled_buffer_14
  Register register_1 (.D(I_Odat), .Q({register_1_q, OSHIBKA}), .clk(and_16_out));  // open: en, clr
  Register register_2 (.D(I_Odat), .Q({register_2_q, clk}), .clk(and_17_out));  // open: en, clr
  nor nor_1 (nor_1_out, and_3_out, and_4_out, and_5_out, and_6_out, and_7_out, and_8_out, and_9_out, and_10_out, and_11_out, and_12_out, and_13_out, and_14_out, and_15_out, and_16_out, and_17_out);
  Register register_3 (.D(I_Odat), .Q({register_3_q, YES_NO_APPLE}), .clk(and_3_out));  // open: en, clr
  and and_18 (RAM, nor_1_out, DATA);
  // Probe on multiplexer_1_out
  // Probe on multiplexer_2_out
  // Probe on multiplexer_3_out
  // Probe on multiplexer_4_out
  // Probe on multiplexer_5_out
  // Probe on multiplexer_6_out
  // Probe on multiplexer_7_out
  // Probe on multiplexer_8_out
  Multiplexer #(.width(8), .enable("false")) multiplexer_1 (
    .in0({8{1'b1}}), .in1({{5{1'b0}}, X_second_Pos}), .out(multiplexer_1_out), .sel(comparator_1_gt));
  Comparator #(.width(4), .mode("unsigned")) comparator_1 (
    .a(in_2), .b(4'b0001), .gt(comparator_1_gt));  // open: eq, lt
  Multiplexer #(.width(8), .enable("false")) multiplexer_2 (
    .in0({8{1'b1}}), .in1({{5{1'b0}}, Y_second_Pos}), .out(multiplexer_2_out), .sel(comparator_2_gt));
  Comparator #(.width(4), .mode("unsigned")) comparator_2 (
    .a(in_2), .b(4'b0001), .gt(comparator_2_gt));  // open: eq, lt
  Multiplexer #(.width(8), .enable("false")) multiplexer_3 (
    .in0({8{1'b1}}), .in1({{5{1'b0}}, X_third_Pos}), .out(multiplexer_3_out), .sel(comparator_3_gt));
  Comparator #(.width(4), .mode("unsigned")) comparator_3 (
    .a(in_2), .b(4'b0011), .gt(comparator_3_gt));  // open: eq, lt
  Multiplexer #(.width(8), .enable("false")) multiplexer_4 (
    .in0({8{1'b1}}), .in1({{5{1'b0}}, Y_third_Pos}), .out(multiplexer_4_out), .sel(comparator_4_gt));
  Comparator #(.width(4), .mode("unsigned")) comparator_4 (
    .a(in_2), .b(4'b0011), .gt(comparator_4_gt));  // open: eq, lt
  Multiplexer #(.width(8), .enable("false")) multiplexer_5 (
    .in0({8{1'b1}}), .in1({{5{1'b0}}, X_fourth_Pos}), .out(multiplexer_5_out), .sel(comparator_5_gt));
  Comparator #(.width(4), .mode("unsigned")) comparator_5 (
    .a(in_2), .b(4'b0101), .gt(comparator_5_gt));  // open: eq, lt
  Multiplexer #(.width(8), .enable("false")) multiplexer_6 (
    .in0({8{1'b1}}), .in1({{5{1'b0}}, Y_fourth_Pos}), .out(multiplexer_6_out), .sel(comparator_6_gt));
  Comparator #(.width(4), .mode("unsigned")) comparator_6 (
    .a(in_2), .b(4'b0101), .gt(comparator_6_gt));  // open: eq, lt
  Multiplexer #(.width(8), .enable("false")) multiplexer_7 (
    .in0({8{1'b1}}), .in1({{5{1'b0}}, X_fifth_Pos}), .out(multiplexer_7_out), .sel(comparator_7_gt));
  Comparator #(.width(4), .mode("unsigned")) comparator_7 (
    .a(in_2), .b(4'b0111), .gt(comparator_7_gt));  // open: eq, lt
  Multiplexer #(.width(8), .enable("false")) multiplexer_8 (
    .in0({8{1'b1}}), .in1({{5{1'b0}}, Y_fifth_Pos}), .out(multiplexer_8_out), .sel(comparator_8_gt));
  Comparator #(.width(4), .mode("unsigned")) comparator_8 (
    .a(in_2), .b(4'b0111), .gt(comparator_8_gt));  // open: eq, lt
  // Probe on nothing

  // Other names for the same wires on the sheet: CL = in_1; cond[3:0] = in_2; RD_WR = IN_OUT

  // Notes on the sheet:
  //   contents of rom_1 (hex, n*v repeats v):
  //   cd f0 d3 ff d1 0 ad d3 f1 d1 0 d0 f2 b0 d2 fc ba 72 e1 52 d0 f3 b0 d2 fd ba 72 e1 52 d1 1 ad d3 e1
  //   bf d2 e2 ba f e1 3b a e1 3b d2 1 d1 e2 a6 d1 ff d2 e0 a9 d0 0 a8 ee 42 d0 e0 b0 8c d2 e0 a8 d1 5 71
  //   e1 50 8f d2 e1 ab d1 0 d2 e0 a9 ee 53 ad d1 0 d0 f2 b0 d3 f3 bf d2 f4 ba 72 e1 69 d2 f5 ba 7e e1 69
  //   d1 1 d2 f6 ba 72 e1 77 d2 f7 ba 7e e1 77 d1 1 d2 f8 ba 72 e1 85 d2 f9 ba 7e e1 85 d1 1 d2 fa ba 72
  //   e1 93 d2 fb ba 7e e1 93 d1 1 d3 fe ad d0 e1 b0 d2 1 72 e1 ae d0 f2 b0 d2 0 72 e0 ab d2 7 72 e1 ae d1
  //   1 ad d0 e1 b0 d2 2 72 e1 d1 d0 f2 b0 d2 0 72 e0 ce d2 7 72 e0 ce d0 f3 b0 72 e0 ce d2 0 72 e1 d1 d1
  //   1 ad d0 e1 b0 d2 3 72 e1 f6 d0 f2 b0 d2 1 72 e0 f3 d2 6 72 e0 f3 d0 f3 b0 d2 1 72 e0 f3 d2 6 72 e1
  //   f6 d1 1 ad d3 ff d1 1 ad ee 2 d4
endmodule

// WallDeter
module WallDeterminer (
  input  [1:0] Level,
  input  [7:0] out1,
  input  [7:0] out2,
  input  [7:0] out3,
  input  [7:0] out4,
  input  [7:0] out5,
  input  [7:0] out6,
  input  [7:0] out7,
  input  [7:0] out8,
  output [7:0] out_10,
  output [7:0] out_11,
  output [7:0] out_12,
  output [7:0] out_13,
  output [7:0] out_14,
  output [7:0] out_15,
  output [7:0] out_16,
  output [7:0] out_17
);

  wire not_1_out, not_2_out;
  wire [7:0] multiplexer_1_out, multiplexer_3_out, res_horizontal1, res_horizontal2, res_horizontal3,
       res_horizontal4, res_horizontal5, res_horizontal6, res_horizontal7, res_horizontal8, res_vertical1,
       res_vertical8, ResultValue, value;

  not not_1 (not_1_out, ResultValue[1]);
  not not_2 (not_2_out, ResultValue[6]);
  assign out_10 = out1 | res_vertical1 | res_horizontal1;  // OR_Gate or_1, 8 bits wide
  assign out_11 = out2 | res_horizontal2;  // OR_Gate or_2, 8 bits wide
  assign out_12 = out3 | res_horizontal3;  // OR_Gate or_3, 8 bits wide
  assign out_13 = out4 | res_horizontal4;  // OR_Gate or_4, 8 bits wide
  assign out_14 = out5 | res_horizontal5;  // OR_Gate or_5, 8 bits wide
  assign out_15 = out6 | res_horizontal6;  // OR_Gate or_6, 8 bits wide
  assign out_16 = out7 | res_horizontal7;  // OR_Gate or_7, 8 bits wide
  assign out_17 = out8 | res_vertical8 | res_horizontal8;  // OR_Gate or_8, 8 bits wide
  Transistor #(.gate("br")) transistor_1 (.in(value[0]), .out(ResultValue[0]), .gate(not_1_out));
  Transistor transistor_2 (.in(value[7]), .out(ResultValue[7]), .gate(not_2_out));
  Multiplexer #(.select(2), .width(8), .enable("false")) multiplexer_1 (
    .in0({8{1'b0}}), .out(multiplexer_1_out), .sel(Level));  // open: in1, in2, in3
  assign res_vertical1 = out1 | multiplexer_1_out;  // OR_Gate or_9, 8 bits wide
  assign res_vertical8 = multiplexer_1_out | out8;  // OR_Gate or_10, 8 bits wide
  Multiplexer #(.select(2), .width(8), .enable("false")) multiplexer_2 (
    .in0({8{1'b0}}), .in1({8{1'b0}}), .in2(8'h81), .out({value[7], ResultValue[6:1], value[0]}), .sel(Level));  // open: in3
  Multiplexer #(.select(2), .width(8), .enable("false")) multiplexer_3 (
    .in0({8{1'b0}}), .in1({8{1'b0}}), .in2(ResultValue), .in3({8{1'b0}}), .out(multiplexer_3_out), .sel(Level));
  assign res_horizontal2 = out2 | multiplexer_3_out;  // OR_Gate or_11, 8 bits wide
  assign res_horizontal3 = out3 | multiplexer_3_out;  // OR_Gate or_12, 8 bits wide
  assign res_horizontal4 = out4 | multiplexer_3_out;  // OR_Gate or_13, 8 bits wide
  assign res_horizontal5 = multiplexer_3_out | out5;  // OR_Gate or_14, 8 bits wide
  assign res_horizontal6 = multiplexer_3_out | out6;  // OR_Gate or_15, 8 bits wide
  assign res_horizontal7 = multiplexer_3_out | out7;  // OR_Gate or_16, 8 bits wide
  assign res_horizontal8 = multiplexer_3_out | out8;  // OR_Gate or_17, 8 bits wide
  assign res_horizontal1 = out1 | multiplexer_3_out;  // OR_Gate or_18, 8 bits wide
  // NAND_Gate nand_1 is placed but not wired

  // Other names for the same wires on the sheet: value[6:1] = ResultValue[6:1]
endmodule

// FinalDis
module FinalDisplay (
  input  [1:0] GameRes,
  input  [7:0] out1,
  input  [7:0] out2,
  input  [7:0] out3,
  input  [7:0] out4,
  input  [7:0] out5,
  input  [7:0] out6,
  input  [7:0] out7,
  input  [7:0] out8,
  output StopClock,
  output [7:0] out_11,
  output [7:0] out_12,
  output [7:0] out_13,
  output [7:0] out_14,
  output [7:0] out_15,
  output [7:0] out_16,
  output [7:0] out_17,
  output [7:0] out_18
);

  Multiplexer #(.select(2), .width(8), .enable("false")) multiplexer_1 (
    .in0(out1), .in1(8'h3c), .in2(8'h3c), .out(out_11), .sel(GameRes));  // open: in3
  Multiplexer #(.select(2), .width(8), .enable("false")) multiplexer_2 (
    .in0(out2), .in1(8'h42), .in2(8'h42), .out(out_12), .sel(GameRes));  // open: in3
  Multiplexer #(.select(2), .width(8), .enable("false")) multiplexer_3 (
    .in0(out3), .in1(8'ha5), .in2(8'ha9), .out(out_13), .sel(GameRes));  // open: in3
  Multiplexer #(.select(2), .width(8), .enable("false")) multiplexer_4 (
    .in0(out4), .in1(8'h89), .in2(8'h85), .out(out_14), .sel(GameRes));  // open: in3
  Multiplexer #(.select(2), .width(8), .enable("false")) multiplexer_5 (
    .in0(out5), .in1(8'h89), .in2(8'h85), .out(out_15), .sel(GameRes));  // open: in3
  Multiplexer #(.select(2), .width(8), .enable("false")) multiplexer_6 (
    .in0(out6), .in1(8'ha5), .in2(8'ha9), .out(out_16), .sel(GameRes));  // open: in3
  Multiplexer #(.select(2), .width(8), .enable("false")) multiplexer_7 (
    .in0(out7), .in1(8'h42), .in2(8'h42), .out(out_17), .sel(GameRes));  // open: in3
  Multiplexer #(.select(2), .width(8), .enable("false")) multiplexer_8 (
    .in0(out8), .in1(8'h3c), .in2(8'h3c), .out(out_18), .sel(GameRes));  // open: in3
  Multiplexer #(.select(2), .enable("false")) multiplexer_9 (
    .in0(1'b0), .in1(1'b1), .in2(1'b1), .out(StopClock), .sel(GameRes));  // open: in3
endmodule

module PreMain (
  input  Tact,
  input  IsKeyPressed,
  input  [6:0] CurrentKey,
  output [7:0] out_4,
  output [7:0] out_5,
  output [7:0] out_6,
  output [7:0] out_7,
  output [7:0] out_8,
  output [7:0] out_9,
  output [7:0] out_10,
  output [7:0] out_11,
  output Clock,
  output out_13
);

  wire and_1_out, and_2_out, and_3_out, and_4_out, and_5_out, and_6_out, and_7_out, and_9_out,
       AssemblerRes_IsEaten, comparator_1_eq, comparator_1_gt, comparator_2_eq, comparator_2_gt,
       comparator_3_lt, comparator_4_eq, comparator_5_eq, comparator_6_eq, comparator_7_eq, comparator_8_eq,
       comparator_9_eq, comparator_10_eq, comparator_11_eq, comparator_12_eq, comparator_13_eq,
       comparator_14_eq, finaldisplay_1_stopclock, IsLevelChanged, IsOver, multiplexer_1_out,
       multiplexer_2_out, multiplexer_3_out, multiplexer_4_out, not_1_out, not_2_out, not_3_out, not_4_out,
       not_5_out, not_6_out, not_7_out, not_8_out, not_9_out, or_1_out, or_2_out, or_3_out, or_4_out,
       or_11_out, processor_1_clk, StopClock, undriven, undriven_2, undriven_3, undriven_4, undriven_5,
       undriven_6, undriven_7, undriven_8, undriven_9, undriven_10, undriven_11, undriven_12;
  wire [1:0] GameRes, Level, multiplexer_10_out, or_5_out, or_6_out;
  wire [2:0] adder_1_out, adder_2_out, adder_3_out, adder_4_out, adder_5_out, AppleXPos3bit, AppleYPos3bit,
       CurrentDirection, CurrentFifthXPos3bit, CurrentFifthYPos3bit, CurrentFirstYPos3bit,
       CurrentFourthXPos3bit, CurrentFourthYPos3bit, CurrentSecondXPos3bit, CurrentSecondYPos3bit,
       CurrentThirdXPos3bit, CurrentThirdYPos3bit, HeadXPos, HeadYPos, multiplexer_5_out, multiplexer_6_out,
       multiplexer_7_out, multiplexer_8_out, multiplexer_9_out, multiplexer_11_out;
  wire [3:0] Condition;
  wire [7:0] apple1, apple2, apple3, apple4, apple5, apple6, apple7, apple8, CurrentFifthYPos8bit,
       CurrentFirstYPos8bit, CurrentFourthYPos8bit, CurrentSecondYPos8bit, CurrentThirdYPos8bit, fifth1,
       fifth2, fifth3, fifth4, fifth5, fifth6, fifth7, fifth8, first1, first2, first3, first4, first5,
       first6, first7, first8, fourth1, fourth2, fourth3, fourth4, fourth5, fourth6, fourth7, fourth8,
       PreFinalRes1, PreFinalRes2, PreFinalRes3, PreFinalRes4, PreFinalRes5, PreFinalRes6, PreFinalRes7,
       PreFinalRes8, second1, second2, second3, second4, second5, second6, second7, second8, TempOut1,
       TempOut2, TempOut3, TempOut4, TempOut5, TempOut6, TempOut7, TempOut8, third1, third2, third3, third4,
       third5, third6, third7, third8;

  LED led_1 (.in(undriven));
  LED led_2 (.in(undriven_2));
  LED led_3 (.in(undriven_4));
  LED led_4 (.in(undriven_3));
  Comparator #(.width(4), .mode("unsigned")) comparator_1 (
    .a(Condition), .b(4'b0000), .gt(comparator_1_gt), .eq(comparator_1_eq));  // open: lt
  Comparator #(.width(4), .mode("unsigned")) comparator_2 (
    .a(Condition), .b(4'b0000), .gt(comparator_2_gt), .eq(comparator_2_eq));  // open: lt
  not not_1 (not_1_out, StopClock);
  Comparator #(.width(4), .mode("unsigned")) comparator_3 (
    .a(Condition), .b(4'b0001), .lt(comparator_3_lt));  // open: gt, eq
  not not_2 (not_2_out, comparator_3_lt);
  Multiplexer #(.enable("false")) multiplexer_1 (
    .in0(1'b0), .in1(1'b1), .out(multiplexer_1_out), .sel(comparator_1_gt));
  Multiplexer #(.enable("false")) multiplexer_2 (
    .in0(1'b0), .in1(1'b0), .out(multiplexer_2_out), .sel(comparator_1_eq));
  Multiplexer #(.enable("false")) multiplexer_3 (
    .in0(1'b0), .in1(1'b1), .out(multiplexer_3_out), .sel(comparator_2_gt));
  Multiplexer #(.enable("false")) multiplexer_4 (
    .in0(1'b0), .in1(1'b0), .out(multiplexer_4_out), .sel(comparator_2_eq));
  Comparator #(.width(7), .mode("unsigned")) comparator_4 (
    .a(CurrentKey), .b(7'b1110111), .eq(comparator_4_eq));  // open: gt, lt
  Comparator #(.width(3), .mode("unsigned")) comparator_5 (
    .a(CurrentDirection), .b(3'b010), .eq(comparator_5_eq));  // open: gt, lt
  Comparator #(.width(7), .mode("unsigned")) comparator_6 (
    .a(CurrentKey), .b(7'b1100100), .eq(comparator_6_eq));  // open: gt, lt
  Comparator #(.width(3), .mode("unsigned")) comparator_7 (
    .a(CurrentDirection), .b(3'b001), .eq(comparator_7_eq));  // open: gt, lt
  Comparator #(.width(7), .mode("unsigned")) comparator_8 (
    .a(CurrentKey), .b(7'b1110011), .eq(comparator_8_eq));  // open: gt, lt
  Comparator #(.width(3), .mode("unsigned")) comparator_9 (
    .a(CurrentDirection), .b(3'b100), .eq(comparator_9_eq));  // open: gt, lt
  Comparator #(.width(7), .mode("unsigned")) comparator_10 (
    .a(CurrentKey), .b(7'b1100001), .eq(comparator_10_eq));  // open: gt, lt
  Comparator #(.width(3), .mode("unsigned")) comparator_11 (
    .a(CurrentDirection), .b(3'b011), .eq(comparator_11_eq));  // open: gt, lt
  Adder #(.width(3)) adder_1 (.a({1'b0, CurrentKey[2:1]}), .b(3'b001), .out(adder_1_out));  // open: cin, cout
  and and_1 (and_1_out, Tact, not_1_out);
  and and_2 (and_2_out, AssemblerRes_IsEaten, not_2_out);
  Multiplexer #(.width(3), .enable("false")) multiplexer_5 (
    .in0(3'b011), .in1(multiplexer_7_out), .out(multiplexer_5_out), .sel(or_1_out));
  or or_1 (or_1_out, multiplexer_1_out, multiplexer_2_out);
  Multiplexer #(.width(3), .enable("false")) multiplexer_6 (
    .in0(3'b100), .in1(multiplexer_8_out), .out(multiplexer_6_out), .sel(or_2_out));
  or or_2 (or_2_out, multiplexer_3_out, multiplexer_4_out);
  not not_3 (not_3_out, comparator_5_eq);
  not not_4 (not_4_out, comparator_7_eq);
  not not_5 (not_5_out, comparator_9_eq);
  not not_6 (not_6_out, comparator_11_eq);
  Processor processor_1 (
    .YES_NO_APPLE(AssemblerRes_IsEaten), .HeadX(HeadXPos), .HeadY(HeadYPos),
    .X_second_Pos(CurrentSecondXPos3bit), .X_third_Pos(CurrentThirdXPos3bit),
    .Y_third_Pos(CurrentThirdYPos3bit), .Y_fourth_Pos(CurrentFourthYPos3bit),
    .X_fifth_Pos(CurrentFifthXPos3bit), .Y_fifth_Pos(CurrentFifthYPos3bit), .AppleX(AppleXPos3bit),
    .AppleY(AppleYPos3bit), .in_1(and_1_out), .OSHIBKA(out_13), .clk(processor_1_clk), .in_2(Condition),
    .Y_second_Pos(CurrentSecondYPos3bit), .X_fourth_Pos(CurrentFourthXPos3bit));
  Comparator #(.width(4), .mode("unsigned")) comparator_12 (
    .a(Condition), .b(4'b0000), .eq(comparator_12_eq));  // open: gt, lt
  Comparator #(.width(4), .mode("unsigned")) comparator_13 (
    .a(Condition), .b(4'b1010), .eq(comparator_13_eq));  // open: gt, lt
  ConditionLevelDeterminer conditionleveldeterminer_1 (
    .AssemblerRes(and_2_out), .Clock(Clock), .Condition(Condition), .Level(Level), .Condition_2(Condition),
    .Level_2(Level), .IsLevelChanged(IsLevelChanged));
  Register #(.width(3)) register_1 (.D(multiplexer_5_out), .en(1'b1), .Q(HeadXPos), .clk(Clock));  // open: clr
  Register #(.width(3)) register_2 (.D(multiplexer_6_out), .en(1'b1), .Q(HeadYPos), .clk(Clock));  // open: clr
  and and_3 (and_3_out, comparator_4_eq, not_3_out);
  and and_4 (and_4_out, comparator_6_eq, not_4_out);
  and and_5 (and_5_out, comparator_8_eq, not_5_out);
  and and_6 (and_6_out, comparator_10_eq, not_6_out);
  not not_7 (not_7_out, comparator_12_eq);
  not not_8 (not_8_out, comparator_13_eq);
  Adder #(.width(3)) adder_2 (.a(3'b111), .b(HeadXPos), .out(adder_2_out));  // open: cin, cout
  Adder #(.width(3)) adder_3 (.a(HeadXPos), .b(3'b001), .out(adder_3_out));  // open: cin, cout
  Adder #(.width(3)) adder_4 (.a(HeadYPos), .b(3'b111), .out(adder_4_out));  // open: cin, cout
  Adder #(.width(3)) adder_5 (.a(HeadYPos), .b(3'b001), .out(adder_5_out));  // open: cin, cout
  or or_3 (or_3_out, and_3_out, and_4_out, and_5_out, and_6_out);
  not not_9 (not_9_out, StopClock);
  and and_7 (and_7_out, out_13, not_7_out, not_8_out);
  LED led_5 (.in(undriven_5));
  Multiplexer #(.select(3), .width(3), .enable("false")) multiplexer_7 (
    .in1(adder_2_out), .in3(adder_3_out), .out(multiplexer_7_out), .sel(CurrentDirection));  // open: in0, in2, in4, in5, in6, in7
  Multiplexer #(.select(3), .width(3), .enable("false")) multiplexer_8 (
    .in2(adder_4_out), .in4(adder_5_out), .out(multiplexer_8_out), .sel(CurrentDirection));  // open: in0, in1, in3, in5, in6, in7
  and and_8 (Clock, processor_1_clk, not_9_out);
  or or_4 (or_4_out, and_7_out, IsOver);
  and and_9 (and_9_out, or_3_out, IsKeyPressed);
  Register #(.width(1)) register_3 (.D(or_4_out), .en(1'b1), .Q(IsOver), .clk(Clock));  // open: clr
  Comparator #(.width(2), .mode("unsigned")) comparator_14 (
    .a(Level), .b(2'b11), .eq(comparator_14_eq));  // open: gt, lt
  LED led_6 (.in(undriven_6));
  LED led_7 (.in(undriven_7));
  Multiplexer #(.width(3), .enable("false")) multiplexer_9 (
    .in0(CurrentDirection), .in1(adder_1_out), .out(multiplexer_9_out), .sel(and_9_out));
  assign or_5_out = {1'b0, IsOver} | 2'b00;  // OR_Gate or_5, 2 bits wide
  Multiplexer #(.width(2), .enable("false")) multiplexer_10 (
    .in0(or_5_out), .in1(2'b10), .out(multiplexer_10_out), .sel(comparator_14_eq));
  GetYPositions getypositions_1 (
    .HeadYPos(HeadYPos), .Clock(Clock), .Condition(Condition), .CurrentFirstPos8bit(CurrentFirstYPos8bit),
    .CurrentFirstPos3bit(CurrentFirstYPos3bit), .CurrentSecondPos8bit(CurrentSecondYPos8bit),
    .CurrentSecondPos3bit(CurrentSecondYPos3bit), .CurrentThirdPos8bit(CurrentThirdYPos8bit),
    .CurrentThirdPos3bit(CurrentThirdYPos3bit), .CurrentFourthPos8bit(CurrentFourthYPos8bit),
    .CurrentFourthPos3bit(CurrentFourthYPos3bit), .CurrentFifthPos8bit(CurrentFifthYPos8bit),
    .CurrentFifthPos3bit(CurrentFifthYPos3bit));
  GetXPositions getxpositions_1 (
    .HeadXPos(HeadXPos), .Clock(Clock), .Condition(Condition), .CurrentSecondPos3bit(CurrentSecondXPos3bit),
    .CurrentThirdPos3bit(CurrentThirdXPos3bit), .CurrentFourthPos3bit(CurrentFourthXPos3bit),
    .CurrentFifthPos3bit(CurrentFifthXPos3bit));
  Multiplexer #(.width(3), .enable("false")) multiplexer_11 (
    .in0(multiplexer_9_out), .in1(3'b000), .out(multiplexer_11_out), .sel(IsLevelChanged));
  Register #(.width(3)) register_4 (.D(multiplexer_11_out), .en(1'b1), .Q(CurrentDirection), .clk(Clock));  // open: clr
  assign or_6_out = GameRes | multiplexer_10_out;  // OR_Gate or_6, 2 bits wide
  Demultiplexer #(.select(3), .width(8), .enable("false")) demultiplexer_1 (
    .out0(first1), .out1(first2), .out2(first3), .out3(first4), .out4(first5), .out5(first6), .out6(first7),
    .out7(first8), .in(CurrentFirstYPos8bit), .sel(HeadXPos));
  Register #(.width(2)) register_5 (.D(or_6_out), .en(1'b1), .Q(GameRes), .clk(Clock));  // open: clr
  LED led_8 (.in(undriven_9));
  LED led_9 (.in(undriven_12));
  LED led_10 (.in(undriven_8));
  LED led_11 (.in(undriven_10));
  LED led_12 (.in(undriven_11));
  AppleCoordinatesGenerator applecoordinatesgenerator_1 (
    .Clock(Clock), .Level(Level), .Condition(Condition), .AppleYPos(AppleYPos3bit),
    .AppleXPos(AppleXPos3bit), .out1(apple1), .out2(apple2), .out3(apple3), .out4(apple4), .out5(apple5),
    .out6(apple6), .out7(apple7), .out8(apple8));
  assign TempOut1 = first1 | second1 | third1 | fourth1 | fifth1 | apple1;  // OR_Gate or_7, 8 bits wide
  assign TempOut2 = first2 | second2 | third2 | fourth2 | fifth2 | apple2;  // OR_Gate or_8, 8 bits wide
  assign TempOut3 = first3 | second3 | third3 | fourth3 | fifth3 | apple3;  // OR_Gate or_9, 8 bits wide
  assign TempOut4 = first4 | second4 | third4 | fourth4 | fifth4 | apple4;  // OR_Gate or_10, 8 bits wide
  WallDeterminer walldeterminer_1 (
    .Level(Level), .out1(TempOut1), .out2(TempOut2), .out3(TempOut3), .out4(TempOut4), .out5(TempOut5),
    .out6(TempOut6), .out7(TempOut7), .out8(TempOut8), .out_10(PreFinalRes1), .out_11(PreFinalRes2),
    .out_12(PreFinalRes3), .out_13(PreFinalRes4), .out_14(PreFinalRes5), .out_15(PreFinalRes6),
    .out_16(PreFinalRes7), .out_17(PreFinalRes8));
  FinalDisplay finaldisplay_1 (
    .GameRes(GameRes), .out1(PreFinalRes1), .out2(PreFinalRes2), .out3(PreFinalRes3), .out4(PreFinalRes4),
    .out5(PreFinalRes5), .out6(PreFinalRes6), .out7(PreFinalRes7), .out8(PreFinalRes8),
    .StopClock(finaldisplay_1_stopclock), .out_11(out_4), .out_12(out_5), .out_13(out_6), .out_14(out_7),
    .out_15(out_8), .out_16(out_9), .out_17(out_10), .out_18(out_11));
  GetBitsFromPos getbitsfrompos_1 (
    .CheckValue(4'b0010), .Condition(Condition), .XPos3bit(CurrentSecondXPos3bit),
    .YPos8bit(CurrentSecondYPos8bit), .out_5(second1), .out_6(second2), .out_7(second3), .out_8(second4),
    .out_9(second5), .out_10(second6), .out_11(second7), .out_12(second8));
  GetBitsFromPos getbitsfrompos_2 (
    .CheckValue(4'b0100), .Condition(Condition), .XPos3bit(CurrentThirdXPos3bit),
    .YPos8bit(CurrentThirdYPos8bit), .out_5(third1), .out_6(third2), .out_7(third3), .out_8(third4),
    .out_9(third5), .out_10(third6), .out_11(third7), .out_12(third8));
  GetBitsFromPos getbitsfrompos_3 (
    .CheckValue(4'b0110), .Condition(Condition), .XPos3bit(CurrentFourthXPos3bit),
    .YPos8bit(CurrentFourthYPos8bit), .out_5(fourth1), .out_6(fourth2), .out_7(fourth3), .out_8(fourth4),
    .out_9(fourth5), .out_10(fourth6), .out_11(fourth7), .out_12(fourth8));
  GetBitsFromPos getbitsfrompos_4 (
    .CheckValue(4'b1000), .Condition(Condition), .XPos3bit(CurrentFifthXPos3bit),
    .YPos8bit(CurrentFifthYPos8bit), .out_5(fifth1), .out_6(fifth2), .out_7(fifth3), .out_8(fifth4),
    .out_9(fifth5), .out_10(fifth6), .out_11(fifth7), .out_12(fifth8));
  or or_11 (or_11_out, StopClock, finaldisplay_1_stopclock);
  assign TempOut5 = first5 | second5 | third5 | fourth5 | fifth5 | apple5;  // OR_Gate or_12, 8 bits wide
  assign TempOut6 = first6 | second6 | third6 | fourth6 | fifth6 | apple6;  // OR_Gate or_13, 8 bits wide
  assign TempOut7 = first7 | second7 | third7 | fourth7 | fifth7 | apple7;  // OR_Gate or_14, 8 bits wide
  assign TempOut8 = first8 | second8 | third8 | fourth8 | fifth8 | apple8;  // OR_Gate or_15, 8 bits wide
  Register #(.width(1)) register_6 (.D(or_11_out), .en(1'b1), .Q(StopClock), .clk(Clock));  // open: clr

  // Other names for the same wires on the sheet: FinalOut1[7:0] = out_4; FinalOut2[7:0] = out_5;
  //   FinalOut3[7:0] = out_6; FinalOut4[7:0] = out_7; FinalOut5[7:0] = out_8; FinalOut6[7:0] = out_9;
  //   FinalOut7[7:0] = out_10; FinalOut8[7:0] = out_11

  // Notes on the sheet:
  //   determining the position of the snake's head
  //   a-61
  //   d - 64
  //   w-77
  //   s - 73
  //   w - 100
  //   d - 011
  //   s - 010
  //   a - 001
  //   defines CurrentDirection
endmodule
